# Fritzing sketch schema_electronique_MedBoxAI (saved by Fritzing 1.0.1rc)

parts:
  SparkFun_ESP32_Thing1 = SparkFun ESP32 Thing [part_number=DEV-13907]
  Composant1 = PN532 Elechouse RFID NFC Module V3
  U1 = MLX90614 [package=to-39]
  Grove1 = Grove OLED 128x96
  M1 = GY-MAX30102
  J1 = Piezo Speaker

nets:
  GND: SparkFun_ESP32_Thing1.GND, Composant1.GND, U1.VSS, Grove1.GND, M1.GND, J1.pin1
  N1: SparkFun_ESP32_Thing1.13, J1.pin2
  VCC: SparkFun_ESP32_Thing1.3.3V, Composant1.VCC, U1.VDD, Grove1.VCC, M1.VIN
  N2: SparkFun_ESP32_Thing1.22, Composant1.SDA, U1.PWM_SDA, Grove1.SDA, M1.SDA
  N3: SparkFun_ESP32_Thing1.21, Composant1.SCL, U1.SCL_VZ, Grove1.SCL, M1.SCL

custom parts:
  SparkFun ESP32 Thing: The SparkFun ESP32 Thing is a comprehensive development platform for Espressif’s ESP32, their super-charged version of the popular ESP8266. Like the 8266, the ESP32 is a WiFi-compatible microcontroller, but to that it adds support for Bluetooth low-energy (i.e BLE, BT4.0, Bluetooth Smart), and nearly 30 I/O pins. The ESP32’s power and versatility will make it the foundation of IoT and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
  PN532 Elechouse RFID NFC Module V3: NFC is a popular technology in recent years. We often heard this work while smart phone company such as Samsung or HTC introduces their latest high-end phones. Almost all the high-end phone in the market support NFC. Near field communication (NFC) is a set of standards for smart phones and similar devices to establish radio communication with each other by touching them together or bringing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
  GY-MAX30102: Oximeter module using the MAX30102 chip. You may wish to read (and check your module) this post on power problems with these modules: https://reedpaper.wordpress.com/2018/08/22/pulse-oximeter-max30100-max30102-how-to-fix-wrong-board/ (may not apply as this is a different module!). As usual, if you want the mounting holes in pcb, you need to drag a hole over the pad in silkscreen to actually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
